// Digital circuit lab2_part2.dig as structural Verilog
module lab2_part2 (
  input  in0,
  input  in1,
  input  in2,
  input  in3,
  output seg_a,
  output seg_f,
  output seg_b,
  output seg_g,
  output seg_e,
  output seg_c,
  output seg_d,
  output seg_dp,
  output sign_a,
  output sign_f,
  output sign_b,
  output sign_g,
  output sign_e,
  output sign_c,
  output sign_d,
  output sign_dp
);

  wire and_1_out, and_2_out;

  Seven_Seg seven_seg_1 (
    .a(sign_a), .b(sign_b), .c(sign_c), .d(sign_d), .e(sign_e), .f(sign_f), .g(sign_g), .dp(sign_dp));
  Seven_Seg seven_seg_2 (.a(seg_a), .b(seg_b), .c(seg_c), .d(seg_d), .e(seg_e), .f(seg_f), .g(seg_g), .dp(seg_dp));
  // XOr xor_1 is placed but not wired
  // XOr xor_2 is placed but not wired
  // And and_1 has open pins: In_1=open, In_2=open, out=and_1_out
  // And and_2 has open pins: In_1=open, In_2=open, out=and_2_out
  // XOr xor_3 has open pins: In_1=and_1_out, In_2=and_2_out, out=open

  // Notes on the sheet:
  //   Interface (do not edit the content inside this box)
  //   Outputs:
  //   Inputs
  //   Sign
  //   Decimal Number
endmodule

/* Test case:
in3 in2 in1 in0  sign_a sign_b sign_c sign_d sign_e sign_f sign_g  seg_a seg_b seg_c seg_d seg_e seg_f seg_g
 0   0   0   0    0      0      0      0      0      0      0       1     1     1     1     1     1     0
*/
